# Fritzing sketch door (saved by Fritzing 0.9.3b)

parts:
  Part6 = NRF24L01+ Breakout Board
  Part7 = Arduino Nano (Rev3.0) (ICSP)
  J3 = Piezo Speaker
  LED3 = RGB LED (com. cathode, rgb) [package="5 mm [THT]"]
  S4 = Reed switch [package=THT]

nets:
  GND: Part6.GND, Part7.GND, J3.pin1, LED3.common_cathode, S4.pin_2
  VCC: Part6.VCC, Part7.3V3
  N1: Part6.CE, Part7.D7
  N2: Part6.CS, Part7.D8
  N3: Part6.SCK, Part7.D13/SCK
  N4: Part6.MOSI, Part7.D11/MOSI
  N5: Part6.MISO, Part7.D12/MISO
  N6: Part7.D2, S4.pin_1
  N7: Part7.D3, LED3.blue_anode
  N8: Part7.D4, LED3.green_anode
  N9: Part7.D5, LED3.red_anode
  N10: Part7.D6, J3.pin2
